# Fritzing sketch WDI Fritzing (saved by Fritzing 0.9.3b)
perfboards: 1

parts:
  Power_plug1 = Power plug  # not connected
  U2 = Voltage Regulator - 5V [package="DPak [SMD]"]  # not connected
  SW-1 = Vibration sensor module  # not connected
  SW-2 = Vibration sensor module  # not connected
  U1 = NodeMCU V3.0
  Q1 = npn-Powertransistor [package="TO220 [THT]"]  # not connected
  Q2 = npn-Powertransistor [package="TO220 [THT]"]  # not connected
  Q4 = npn-Powertransistor [package="TO220 [THT]"]  # not connected
  R3 = Resistor [tolerance=±5% resistance=220 package="2512 [SMD]"]
  R4 = Resistor [tolerance=±5% resistance=220 package="2512 [SMD]"]
  R5 = Resistor [tolerance=±5% resistance=220 package="2512 [SMD]"]
  Q3 = npn-Powertransistor [package="TO220 [THT]"]  # not connected
  PIR1 = PIR sensor
  R1 = Resistor [tolerance=±5% resistance=220 package="2512 [SMD]"]

nets:
  N1: U1.D0, PIR1.SIG
  N2: U1.D1, R4.Pin_1
  N3: U1.D2, R3.Pin_1
  3V3: U1.3V3, PIR1.VDD
  N4: U1.GND#6, U1.GND#13, U1.GND#16, U1.GND#33
  N5: U1.D5, R5.Pin_1
  N6: U1.D6, R1.Pin_1

custom parts:
  Vibration sensor module: Single-roller type full induction trigger switch. When no vibration or tilt, the product is ON conduction state, and in the steady state, when a vibration or tilt, the switch will be rendered instantly disconnect the conductive resistance increases, generating a current pulse signal, thereby triggering circuit. The default state of the swith is close Digital output Supply voltage:3.3V-5V On-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
  NodeMCU V3.0: ESP8266 based NodeMCU
